# Fritzing sketch tank (saved by Fritzing 0.9.6b)
breadboards: 1

parts:
  MCU1 = Raspberry Pi Zero
  S1 = Pushbutton [package="[THT]"]
  LED1 = LED - 5mm [color="Red (633nm)" current=0.030 package="5 mm [THT]"]
  EDGY_motor_control1 = EDGY [part_number=L298N]
  M1 = DC Motor
  M2 = DC Motor
  HC-SR04_Sensor_1 = HC-SR04 Ultrasonic Distance Sensor
  R1 = Resistor [tolerance=±5% resistance=220 package="2010 [SMD]"]
  R2 = Resistor [tolerance=±5% resistance=470 package="2010 [SMD]"]
  DC1 = DC_DC_XL4016 [package=board_screw]
  Power_plug1 = Power plug
  S2 = Taiway 100-SP-X-T1 SPDT Miniature Toggle Switch [part_number=100-SP-X-T1-0-0-B1-M1 package=THT]
  R3 = Resistor [tolerance=±5% resistance=220 package="2010 [SMD]"]
  R4 = Resistor [tolerance=±5% resistance=220 package="2010 [SMD]"]

nets:
  N1: MCU1.pin_2, MCU1.pin_4, HC-SR04_Sensor_1.VCC, DC1.OUT+
  N2: MCU1.pin_6, MCU1.pin_14, MCU1.pin_34, LED1.cathode, HC-SR04_Sensor_1.GND, R2.Pin_1, DC1.OUT-, R4.Pin_1
  N3: MCU1.pin_10, R3.Pin_1
  N4: MCU1.pin_12, S1.Pin_3, S1.Pin_4, R4.Pin_0
  N5: MCU1.pin_16, EDGY_motor_control1.B1
  N6: MCU1.pin_18, EDGY_motor_control1.A1
  N7: MCU1.pin_19, EDGY_motor_control1.Speed2
  N8: MCU1.pin_21, EDGY_motor_control1.B2
  N9: MCU1.pin_22, EDGY_motor_control1.Speed1
  N10: MCU1.pin_23, EDGY_motor_control1.A2
  N11: MCU1.pin_38, HC-SR04_Sensor_1.TRIG
  N12: MCU1.pin_40, R1.Pin_1, R2.Pin_0
  N13: S1.Pin_1, S1.Pin_2
  N14: LED1.anode, R3.Pin_0
  N15: EDGY_motor_control1.B2out, M1.pin_2
  N16: EDGY_motor_control1.A2out, M1.pin_1
  N17: EDGY_motor_control1.B1out, M2.pin_2
  N18: EDGY_motor_control1.A1out, M2.pin_1
  GND: EDGY_motor_control1.GND, DC1.IN-, Power_plug1.GND
  N19: EDGY_motor_control1.5V+, DC1.IN+, S2.L2
  N20: HC-SR04_Sensor_1.ECHO, R1.Pin_0
  N21: Power_plug1.VCC, S2.COM

notes:
  L298N motor shield. As I cant find the shield-icon as I bought it, I use this one
  IN1 -> A
  IN2 -> B
  enable -> SP
  Actually an UBEC. 12-24v in, nice flat 5v out. I use 8 AA batteries as a power source.
  yes, yes, gray GND line is silly. I drew this here as a reminder for my set-up in my tank (where I obviously do not use a breadboard)
